// Logisim project 150120006_150121921_524123004_150120942.circ as structural Verilog: 23 circuits, main circuit Microprocessor
module testing (
  input  [9:0] in_1,
  input  [17:0] in_2,
  input  in_3,
  input  in_4,
  input  in_5,
  input  in_6,
  input  in_7,
  output [17:0] out_8
);

  RAM #(.addrWidth(10), .dataWidth(18), .bus("separate")) ram_1 (
    .addr(in_1), .din(in_2), .data(out_8), .str(in_3), .sel(in_5), .clk(in_7), .ld(in_6), .clr(in_4));
endmodule

module D_Flip_Flop (
  input  D,
  input  Clk,
  output Q
);

  wire and_1_out, and_2_out, and_3_out, and_4_out, nor_1_out, nor_2_out, nor_3_out, not_1_out, not_2_out,
       not_3_out;

  not not_1 (not_1_out, D);
  not not_2 (not_2_out, Clk);
  and and_1 (and_1_out, D, not_2_out);
  and and_2 (and_2_out, not_2_out, not_1_out);
  nor nor_1 (nor_1_out, and_1_out, nor_2_out);
  nor nor_2 (nor_2_out, nor_1_out, and_2_out);
  not not_3 (not_3_out, nor_2_out);
  and and_3 (and_3_out, nor_2_out, Clk);
  and and_4 (and_4_out, Clk, not_3_out);
  nor nor_3 (nor_3_out, and_3_out, Q);
  nor nor_4 (Q, nor_3_out, and_4_out);
endmodule

module Register (
  input  [17:0] I,
  input  clk,
  output [17:0] Q
);

  D_Flip_Flop d_flip_flop_1 (.D(I[17]), .Q(Q[17]), .Clk(clk));
  D_Flip_Flop d_flip_flop_2 (.D(I[16]), .Q(Q[16]), .Clk(clk));
  D_Flip_Flop d_flip_flop_3 (.D(I[15]), .Q(Q[15]), .Clk(clk));
  D_Flip_Flop d_flip_flop_4 (.D(I[14]), .Q(Q[14]), .Clk(clk));
  D_Flip_Flop d_flip_flop_5 (.D(I[13]), .Q(Q[13]), .Clk(clk));
  D_Flip_Flop d_flip_flop_6 (.D(I[12]), .Q(Q[12]), .Clk(clk));
  D_Flip_Flop d_flip_flop_7 (.D(I[11]), .Q(Q[11]), .Clk(clk));
  D_Flip_Flop d_flip_flop_8 (.D(I[10]), .Q(Q[10]), .Clk(clk));
  D_Flip_Flop d_flip_flop_9 (.D(I[9]), .Q(Q[9]), .Clk(clk));
  D_Flip_Flop d_flip_flop_10 (.D(I[8]), .Q(Q[8]), .Clk(clk));
  D_Flip_Flop d_flip_flop_11 (.D(I[7]), .Q(Q[7]), .Clk(clk));
  D_Flip_Flop d_flip_flop_12 (.D(I[6]), .Q(Q[6]), .Clk(clk));
  D_Flip_Flop d_flip_flop_13 (.D(I[4]), .Q(Q[4]), .Clk(clk));
  D_Flip_Flop d_flip_flop_14 (.D(I[5]), .Q(Q[5]), .Clk(clk));
  D_Flip_Flop d_flip_flop_15 (.D(I[3]), .Q(Q[3]), .Clk(clk));
  D_Flip_Flop d_flip_flop_16 (.D(I[2]), .Q(Q[2]), .Clk(clk));
  D_Flip_Flop d_flip_flop_17 (.D(I[1]), .Q(Q[1]), .Clk(clk));
  D_Flip_Flop d_flip_flop_18 (.D(I[0]), .Q(Q[0]), .Clk(clk));
endmodule

module Comparator (
  input  [17:0] number_2,
  input  [17:0] number_1,
  output CARRY_FLAG,
  output ZERO_FLAG
);

  wire or_1_out, or_2_out, or_3_out, or_4_out, or_5_out, or_6_out, subtractor_1_new_carry,
       subtractor_1_result, subtractor_2_new_carry, subtractor_2_result, subtractor_3_new_carry,
       subtractor_3_result, subtractor_4_new_carry, subtractor_4_result, subtractor_5_new_carry,
       subtractor_5_result, subtractor_6_new_carry, subtractor_6_result, subtractor_7_new_carry,
       subtractor_7_result, subtractor_8_new_carry, subtractor_8_result, subtractor_9_new_carry,
       subtractor_9_result, subtractor_10_new_carry, subtractor_10_result, subtractor_11_new_carry,
       subtractor_11_result, subtractor_12_new_carry, subtractor_12_result, subtractor_13_new_carry,
       subtractor_13_result, subtractor_14_new_carry, subtractor_14_result, subtractor_15_new_carry,
       subtractor_15_result, subtractor_16_new_carry, subtractor_16_result, subtractor_17_new_carry,
       subtractor_17_result, subtractor_18_new_carry, subtractor_18_result;

  Subtractor subtractor_1 (
    .number_1(number_1[17]), .number_2(number_2[17]), .carry(subtractor_2_new_carry),
    .result(subtractor_1_result), .new_carry(subtractor_1_new_carry));
  and and_1 (CARRY_FLAG, subtractor_1_new_carry, or_4_out);
  Subtractor subtractor_2 (
    .number_1(number_1[16]), .number_2(number_2[16]), .carry(subtractor_4_new_carry),
    .result(subtractor_2_result), .new_carry(subtractor_2_new_carry));
  or or_1 (or_1_out, subtractor_1_result, subtractor_2_result);
  Subtractor subtractor_3 (
    .number_1(number_1[14]), .number_2(number_2[14]), .carry(subtractor_6_new_carry),
    .result(subtractor_3_result), .new_carry(subtractor_3_new_carry));
  Subtractor subtractor_4 (
    .number_1(number_1[15]), .number_2(number_2[15]), .carry(subtractor_3_new_carry),
    .result(subtractor_4_result), .new_carry(subtractor_4_new_carry));
  Subtractor subtractor_5 (
    .number_1(number_1[12]), .number_2(number_2[12]), .carry(subtractor_7_new_carry),
    .result(subtractor_5_result), .new_carry(subtractor_5_new_carry));
  Subtractor subtractor_6 (
    .number_1(number_1[13]), .number_2(number_2[13]), .carry(subtractor_5_new_carry),
    .result(subtractor_6_result), .new_carry(subtractor_6_new_carry));
  or or_2 (or_2_out, subtractor_4_result, subtractor_3_result, subtractor_6_result, subtractor_5_result);
  Subtractor subtractor_7 (
    .number_1(number_1[11]), .number_2(number_2[11]), .carry(subtractor_8_new_carry),
    .result(subtractor_7_result), .new_carry(subtractor_7_new_carry));
  Subtractor subtractor_8 (
    .number_1(number_1[10]), .number_2(number_2[10]), .carry(subtractor_10_new_carry),
    .result(subtractor_8_result), .new_carry(subtractor_8_new_carry));
  Subtractor subtractor_9 (
    .number_1(number_1[8]), .number_2(number_2[8]), .carry(subtractor_11_new_carry),
    .result(subtractor_9_result), .new_carry(subtractor_9_new_carry));
  Subtractor subtractor_10 (
    .number_1(number_1[9]), .number_2(number_2[9]), .carry(subtractor_9_new_carry),
    .result(subtractor_10_result), .new_carry(subtractor_10_new_carry));
  or or_3 (or_3_out, subtractor_7_result, subtractor_8_result, subtractor_10_result, subtractor_9_result);
  or or_4 (or_4_out, or_1_out, or_2_out, or_3_out, or_5_out, or_6_out);
  not not_1 (ZERO_FLAG, or_4_out);
  Subtractor subtractor_11 (
    .number_1(number_1[7]), .number_2(number_2[7]), .carry(subtractor_13_new_carry),
    .result(subtractor_11_result), .new_carry(subtractor_11_new_carry));
  Subtractor subtractor_12 (
    .number_1(number_1[5]), .number_2(number_2[5]), .carry(subtractor_14_new_carry),
    .result(subtractor_12_result), .new_carry(subtractor_12_new_carry));
  Subtractor subtractor_13 (
    .number_1(number_1[6]), .number_2(number_2[6]), .carry(subtractor_12_new_carry),
    .result(subtractor_13_result), .new_carry(subtractor_13_new_carry));
  or or_5 (or_5_out, subtractor_11_result, subtractor_13_result, subtractor_12_result, subtractor_14_result);
  Subtractor subtractor_14 (
    .number_1(number_1[4]), .number_2(number_2[4]), .carry(subtractor_16_new_carry),
    .result(subtractor_14_result), .new_carry(subtractor_14_new_carry));
  Subtractor subtractor_15 (
    .number_1(number_1[2]), .number_2(number_2[2]), .carry(subtractor_18_new_carry),
    .result(subtractor_15_result), .new_carry(subtractor_15_new_carry));
  Subtractor subtractor_16 (
    .number_1(number_1[3]), .number_2(number_2[3]), .carry(subtractor_15_new_carry),
    .result(subtractor_16_result), .new_carry(subtractor_16_new_carry));
  Subtractor subtractor_17 (
    .number_1(number_1[0]), .number_2(number_2[0]), .carry(1'b0), .result(subtractor_17_result),
    .new_carry(subtractor_17_new_carry));
  Subtractor subtractor_18 (
    .number_1(number_1[1]), .number_2(number_2[1]), .carry(subtractor_17_new_carry),
    .result(subtractor_18_result), .new_carry(subtractor_18_new_carry));
  or or_6 (or_6_out, subtractor_16_result, subtractor_15_result, subtractor_18_result, subtractor_17_result);
endmodule

module Subtractor (
  input  number_1,
  input  number_2,
  input  carry,
  output result,
  output new_carry
);

  wire and_1_out, and_2_out, and_3_out, xor_1_out;

  and and_1 (and_1_out, ~number_1, carry);  // AND_Gate
  and and_2 (and_2_out, ~number_1, number_2);  // AND_Gate
  or or_1 (new_carry, and_1_out, and_2_out, and_3_out);
  and and_3 (and_3_out, number_2, carry);
  xor xor_1 (xor_1_out, number_1, number_2);
  xor xor_2 (result, xor_1_out, carry);
endmodule

module Microprocessor (
  output out_1,
  output [17:0] out_2
);

  wire CF_out_4, clock_1_out, comparator_1_p1, comparator_1_p2, undriven, undriven_2, undriven_3, undriven_4,
       ZF_out_4;
  wire [3:0] multiplexer_1_out;
  wire [17:0] comparator_1_p3, comparator_1_p4, Inst_Register_out_4, multiplexer_2_out, multiplexer_3_out,
       pc_1_output, ram_1_data, rom_1_data, signextender6to18bits_1_output_extended_18bits;

  Clock clock_1 (.out(clock_1_out));
  PC pc_1 (.\output (pc_1_output), .Clock(clock_1_out));  // open: input, Jumps_Switch, write, load
  ROM #(.addrWidth(18), .dataWidth(18)) rom_1 (.addr(pc_1_output), .data(rom_1_data), .sel(1'b1));
  flag CF (.in_1(comparator_1_p1), .out_4(CF_out_4), .clk(clock_1_out));  // open: load
  flag ZF (.in_1(comparator_1_p2), .out_4(ZF_out_4), .clk(clock_1_out));  // open: load
  Register_Parallel_Load Inst_Register (
    .in_1(rom_1_data), .load(undriven), .out_4(Inst_Register_out_4), .clk(clock_1_out));
  // Comparator comparator_1: pin names not known; wires that end beside it: comparator_1_p1, comparator_1_p2, comparator_1_p3, comparator_1_p4
  Register_File_Initialised Reg_File (
    .Data_to_Write(multiplexer_2_out), .Reg_No(Inst_Register_out_4[13:10]), .Data_to_Read_1(comparator_1_p3),
    .Data_to_Read_2(comparator_1_p4), .Reg_No_1(multiplexer_1_out), .Reg_No_2(Inst_Register_out_4[3:0]),
    .clk(clock_1_out));  // open: enable_write, initialise
  Multiplexer #(.width(4), .enable("false")) multiplexer_1 (
    .in0(Inst_Register_out_4[9:6]), .in1(Inst_Register_out_4[13:10]), .out(multiplexer_1_out),
    .sel(undriven_3));
  RAM #(.addrWidth(10), .dataWidth(18), .bus("separate")) ram_1 (
    .addr(Inst_Register_out_4[9:0]), .din(comparator_1_p3), .data(ram_1_data), .str(undriven_2), .sel(1'b1),
    .clk(clock_1_out), .ld(1'b1), .clr(1'b0));
  Multiplexer #(.width(18), .enable("false")) multiplexer_2 (
    .in0(ram_1_data), .in1(out_2), .out(multiplexer_2_out), .sel(undriven_4));
  signExtender6To18bits signextender6to18bits_1 (
    .immediate(Inst_Register_out_4[5:0]),
    .output_extended_18bits(signextender6to18bits_1_output_extended_18bits));
  Multiplexer #(.width(18), .enable("false")) multiplexer_3 (
    .in0(comparator_1_p4), .in1(signextender6to18bits_1_output_extended_18bits), .out(multiplexer_3_out),
    .sel(Inst_Register_out_4[16]));
  ALU alu_1 (
    .a(comparator_1_p3), .b(multiplexer_3_out), .carryOut(out_1), .result(out_2),
    ._15th_14th_bit(Inst_Register_out_4[15:14]));

  // Notes on the sheet:
  //   INSTRUCTION MEMO
  //   contents of rom_1 (hex, n*v repeats v):
  //   187fe 840 1cff6 5001 1327b 9001 f909 243f2 4a05 283fc 2c303 3023a 343c1 383f1 20c09
  //   CONTROL UNIT
  //   opcode
  //   DR
  //   addr
  //   SR1
  //   imm
  //   SR2
  //   store to memo
  //   DATA MEMO
endmodule

module Register_Parallel_Load (
  input  [17:0] in_1,
  input  load,
  input  clk,
  output [17:0] out_4
);

  wire [17:0] multiplexer_1_out;

  Multiplexer #(.width(18), .enable("false")) multiplexer_1 (
    .in0(out_4), .in1(in_1), .out(multiplexer_1_out), .sel(load));
  Register register_1 (.I(multiplexer_1_out), .clk(clk), .Q(out_4));
endmodule

module Register_Multifunction (
  input  [17:0] in_1,
  input  [1:0] operation,
  input  clk,
  output [17:0] out_4
);

  wire [17:0] multiplexer_1_out;

  Multiplexer #(.select(2), .width(18), .enable("false")) multiplexer_1 (
    .in0({18{1'b0}}), .in1({18{1'b0}}), .in2(out_4), .in3(in_1), .out(multiplexer_1_out), .sel(operation));
  Register register_1 (.I(multiplexer_1_out), .clk(clk), .Q(out_4));
endmodule

module Register_File (
  input  [17:0] Data_to_Write,
  input  enable_read,
  input  [3:0] Reg_No_1,
  input  [3:0] Reg_No_2,
  input  enable_write,
  input  [3:0] Reg_No,
  input  clk,
  output [17:0] Data_to_Read_1,
  output [17:0] Data_to_Read_2
);

  wire decoder_1_out0, decoder_1_out1, decoder_1_out2, decoder_1_out3, decoder_1_out4, decoder_1_out5,
       decoder_1_out6, decoder_1_out7, decoder_1_out8, decoder_1_out9, decoder_1_out10, decoder_1_out11,
       decoder_1_out12, decoder_1_out13, decoder_1_out14, decoder_1_out15;
  wire [17:0] register_parallel_load_1_out_4, register_parallel_load_2_out_4, register_parallel_load_3_out_4,
       register_parallel_load_4_out_4, register_parallel_load_5_out_4, register_parallel_load_6_out_4,
       register_parallel_load_7_out_4, register_parallel_load_8_out_4, register_parallel_load_9_out_4,
       register_parallel_load_10_out_4, register_parallel_load_11_out_4, register_parallel_load_12_out_4,
       register_parallel_load_13_out_4, register_parallel_load_14_out_4, register_parallel_load_15_out_4,
       register_parallel_load_16_out_4;

  Decoder #(.select(4)) decoder_1 (
    .out0(decoder_1_out0), .out1(decoder_1_out1), .out2(decoder_1_out2), .out3(decoder_1_out3),
    .out4(decoder_1_out4), .out5(decoder_1_out5), .out6(decoder_1_out6), .out7(decoder_1_out7),
    .out8(decoder_1_out8), .out9(decoder_1_out9), .out10(decoder_1_out10), .out11(decoder_1_out11),
    .out12(decoder_1_out12), .out13(decoder_1_out13), .out14(decoder_1_out14), .out15(decoder_1_out15),
    .sel(Reg_No), .en(enable_write));
  Register_Parallel_Load register_parallel_load_1 (
    .in_1(Data_to_Write), .load(decoder_1_out15), .out_4(register_parallel_load_1_out_4), .clk(clk));
  Register_Parallel_Load register_parallel_load_2 (
    .in_1(Data_to_Write), .load(decoder_1_out14), .out_4(register_parallel_load_2_out_4), .clk(clk));
  Register_Parallel_Load register_parallel_load_3 (
    .in_1(Data_to_Write), .load(decoder_1_out13), .out_4(register_parallel_load_3_out_4), .clk(clk));
  Register_Parallel_Load register_parallel_load_4 (
    .in_1(Data_to_Write), .load(decoder_1_out12), .out_4(register_parallel_load_4_out_4), .clk(clk));
  Register_Parallel_Load register_parallel_load_5 (
    .in_1(Data_to_Write), .load(decoder_1_out11), .out_4(register_parallel_load_5_out_4), .clk(clk));
  Register_Parallel_Load register_parallel_load_6 (
    .in_1(Data_to_Write), .load(decoder_1_out10), .out_4(register_parallel_load_6_out_4), .clk(clk));
  Register_Parallel_Load register_parallel_load_7 (
    .in_1(Data_to_Write), .load(decoder_1_out9), .out_4(register_parallel_load_7_out_4), .clk(clk));
  Register_Parallel_Load register_parallel_load_8 (
    .in_1(Data_to_Write), .load(decoder_1_out8), .out_4(register_parallel_load_8_out_4), .clk(clk));
  Register_Parallel_Load register_parallel_load_9 (
    .in_1(Data_to_Write), .load(decoder_1_out7), .out_4(register_parallel_load_9_out_4), .clk(clk));
  Register_Parallel_Load register_parallel_load_10 (
    .in_1(Data_to_Write), .load(decoder_1_out6), .out_4(register_parallel_load_10_out_4), .clk(clk));
  Register_Parallel_Load register_parallel_load_11 (
    .in_1(Data_to_Write), .load(decoder_1_out5), .out_4(register_parallel_load_11_out_4), .clk(clk));
  Register_Parallel_Load register_parallel_load_12 (
    .in_1(Data_to_Write), .load(decoder_1_out4), .out_4(register_parallel_load_12_out_4), .clk(clk));
  Register_Parallel_Load register_parallel_load_13 (
    .in_1(Data_to_Write), .load(decoder_1_out2), .out_4(register_parallel_load_13_out_4), .clk(clk));
  Register_Parallel_Load register_parallel_load_14 (
    .in_1(Data_to_Write), .load(decoder_1_out3), .out_4(register_parallel_load_14_out_4), .clk(clk));
  Register_Parallel_Load register_parallel_load_15 (
    .in_1(Data_to_Write), .load(decoder_1_out1), .out_4(register_parallel_load_15_out_4), .clk(clk));
  Register_Parallel_Load register_parallel_load_16 (
    .in_1(Data_to_Write), .load(decoder_1_out0), .out_4(register_parallel_load_16_out_4), .clk(clk));
  Multiplexer #(.select(4), .width(18)) multiplexer_1 (
    .in0(register_parallel_load_16_out_4), .in1(register_parallel_load_15_out_4),
    .in2(register_parallel_load_13_out_4), .in3(register_parallel_load_14_out_4),
    .in4(register_parallel_load_12_out_4), .in5(register_parallel_load_11_out_4),
    .in6(register_parallel_load_10_out_4), .in7(register_parallel_load_9_out_4),
    .in8(register_parallel_load_8_out_4), .in9(register_parallel_load_7_out_4),
    .in10(register_parallel_load_6_out_4), .in11(register_parallel_load_5_out_4),
    .in12(register_parallel_load_4_out_4), .in13(register_parallel_load_3_out_4),
    .in14(register_parallel_load_2_out_4), .in15(register_parallel_load_1_out_4), .out(Data_to_Read_1),
    .sel(Reg_No_1), .en(enable_read));
  Multiplexer #(.select(4), .width(18)) multiplexer_2 (
    .in0(register_parallel_load_16_out_4), .in1(register_parallel_load_15_out_4),
    .in2(register_parallel_load_13_out_4), .in3(register_parallel_load_14_out_4),
    .in4(register_parallel_load_12_out_4), .in5(register_parallel_load_11_out_4),
    .in6(register_parallel_load_10_out_4), .in7(register_parallel_load_9_out_4),
    .in8(register_parallel_load_8_out_4), .in9(register_parallel_load_7_out_4),
    .in10(register_parallel_load_6_out_4), .in11(register_parallel_load_5_out_4),
    .in12(register_parallel_load_4_out_4), .in13(register_parallel_load_3_out_4),
    .in14(register_parallel_load_2_out_4), .in15(register_parallel_load_1_out_4), .out(Data_to_Read_2),
    .sel(Reg_No_2), .en(enable_read));
endmodule

module Register_File_Initialised (
  input  [17:0] Data_to_Write,
  input  [3:0] Reg_No_1,
  input  [3:0] Reg_No_2,
  input  enable_write,
  input  [3:0] Reg_No,
  input  initialise,
  input  clk,
  output [17:0] Data_to_Read_1,
  output [17:0] Data_to_Read_2
);

  wire decoder_1_out0, decoder_1_out1, decoder_1_out2, decoder_1_out3, decoder_1_out4, decoder_1_out5,
       decoder_1_out6, decoder_1_out7, decoder_1_out8, decoder_1_out9, decoder_1_out10, decoder_1_out11,
       decoder_1_out12, decoder_1_out13, decoder_1_out14, decoder_1_out15, or_1_out, or_2_out, or_3_out,
       or_4_out, or_5_out, or_6_out, or_7_out, or_8_out, or_9_out, or_10_out, or_11_out, or_12_out,
       or_13_out, or_14_out, or_15_out, or_16_out;
  wire [17:0] register_parallel_load_1_out_4, register_parallel_load_2_out_4, register_parallel_load_3_out_4,
       register_parallel_load_4_out_4, register_parallel_load_5_out_4, register_parallel_load_6_out_4,
       register_parallel_load_7_out_4, register_parallel_load_8_out_4, register_parallel_load_9_out_4,
       register_parallel_load_10_out_4, register_parallel_load_11_out_4, register_parallel_load_12_out_4,
       register_parallel_load_13_out_4, register_parallel_load_14_out_4, register_parallel_load_15_out_4,
       register_parallel_load_16_out_4;

  Decoder #(.select(4)) decoder_1 (
    .out0(decoder_1_out0), .out1(decoder_1_out1), .out2(decoder_1_out2), .out3(decoder_1_out3),
    .out4(decoder_1_out4), .out5(decoder_1_out5), .out6(decoder_1_out6), .out7(decoder_1_out7),
    .out8(decoder_1_out8), .out9(decoder_1_out9), .out10(decoder_1_out10), .out11(decoder_1_out11),
    .out12(decoder_1_out12), .out13(decoder_1_out13), .out14(decoder_1_out14), .out15(decoder_1_out15),
    .sel(Reg_No), .en(enable_write));
  Register_Parallel_Load register_parallel_load_1 (
    .in_1(Data_to_Write), .load(or_1_out), .out_4(register_parallel_load_1_out_4), .clk(clk));
  or or_1 (or_1_out, decoder_1_out15, initialise);
  Register_Parallel_Load register_parallel_load_2 (
    .in_1(Data_to_Write), .load(or_2_out), .out_4(register_parallel_load_2_out_4), .clk(clk));
  or or_2 (or_2_out, decoder_1_out14, initialise);
  Register_Parallel_Load register_parallel_load_3 (
    .in_1(Data_to_Write), .load(or_3_out), .out_4(register_parallel_load_3_out_4), .clk(clk));
  or or_3 (or_3_out, decoder_1_out13, initialise);
  Register_Parallel_Load register_parallel_load_4 (
    .in_1(Data_to_Write), .load(or_4_out), .out_4(register_parallel_load_4_out_4), .clk(clk));
  or or_4 (or_4_out, decoder_1_out12, initialise);
  Register_Parallel_Load register_parallel_load_5 (
    .in_1(Data_to_Write), .load(or_5_out), .out_4(register_parallel_load_5_out_4), .clk(clk));
  or or_5 (or_5_out, decoder_1_out11, initialise);
  Register_Parallel_Load register_parallel_load_6 (
    .in_1(Data_to_Write), .load(or_6_out), .out_4(register_parallel_load_6_out_4), .clk(clk));
  Register_Parallel_Load register_parallel_load_7 (
    .in_1(Data_to_Write), .load(or_7_out), .out_4(register_parallel_load_7_out_4), .clk(clk));
  or or_6 (or_6_out, decoder_1_out9, initialise);
  or or_7 (or_7_out, decoder_1_out10, initialise);
  Register_Parallel_Load register_parallel_load_8 (
    .in_1(Data_to_Write), .load(or_8_out), .out_4(register_parallel_load_8_out_4), .clk(clk));
  or or_8 (or_8_out, decoder_1_out8, initialise);
  Register_Parallel_Load register_parallel_load_9 (
    .in_1(Data_to_Write), .load(or_9_out), .out_4(register_parallel_load_9_out_4), .clk(clk));
  or or_9 (or_9_out, decoder_1_out7, initialise);
  Register_Parallel_Load register_parallel_load_10 (
    .in_1(Data_to_Write), .load(or_10_out), .out_4(register_parallel_load_10_out_4), .clk(clk));
  or or_10 (or_10_out, decoder_1_out6, initialise);
  Register_Parallel_Load register_parallel_load_11 (
    .in_1(Data_to_Write), .load(or_11_out), .out_4(register_parallel_load_11_out_4), .clk(clk));
  or or_11 (or_11_out, decoder_1_out5, initialise);
  Register_Parallel_Load register_parallel_load_12 (
    .in_1(Data_to_Write), .load(or_13_out), .out_4(register_parallel_load_12_out_4), .clk(clk));
  or or_12 (or_12_out, decoder_1_out3, initialise);
  or or_13 (or_13_out, decoder_1_out4, initialise);
  Register_Parallel_Load register_parallel_load_13 (
    .in_1(Data_to_Write), .load(or_14_out), .out_4(register_parallel_load_13_out_4), .clk(clk));
  Register_Parallel_Load register_parallel_load_14 (
    .in_1(Data_to_Write), .load(or_12_out), .out_4(register_parallel_load_14_out_4), .clk(clk));
  or or_14 (or_14_out, decoder_1_out2, initialise);
  Register_Parallel_Load register_parallel_load_15 (
    .in_1(Data_to_Write), .load(or_15_out), .out_4(register_parallel_load_15_out_4), .clk(clk));
  or or_15 (or_15_out, decoder_1_out1, initialise);
  Register_Parallel_Load register_parallel_load_16 (
    .in_1(Data_to_Write), .load(or_16_out), .out_4(register_parallel_load_16_out_4), .clk(clk));
  or or_16 (or_16_out, decoder_1_out0, initialise);
  Multiplexer #(.select(4), .width(18), .enable("false")) multiplexer_1 (
    .in0(register_parallel_load_16_out_4), .in1(register_parallel_load_15_out_4),
    .in2(register_parallel_load_13_out_4), .in3(register_parallel_load_14_out_4),
    .in4(register_parallel_load_12_out_4), .in5(register_parallel_load_11_out_4),
    .in6(register_parallel_load_10_out_4), .in7(register_parallel_load_9_out_4),
    .in8(register_parallel_load_8_out_4), .in9(register_parallel_load_6_out_4),
    .in10(register_parallel_load_7_out_4), .in11(register_parallel_load_5_out_4),
    .in12(register_parallel_load_4_out_4), .in13(register_parallel_load_3_out_4),
    .in14(register_parallel_load_2_out_4), .in15(register_parallel_load_1_out_4), .out(Data_to_Read_1),
    .sel(Reg_No_1));
  Multiplexer #(.select(4), .width(18), .enable("false")) multiplexer_2 (
    .in0(register_parallel_load_16_out_4), .in1(register_parallel_load_15_out_4),
    .in2(register_parallel_load_13_out_4), .in3(register_parallel_load_14_out_4),
    .in4(register_parallel_load_12_out_4), .in5(register_parallel_load_11_out_4),
    .in6(register_parallel_load_10_out_4), .in7(register_parallel_load_9_out_4),
    .in8(register_parallel_load_8_out_4), .in9(register_parallel_load_6_out_4),
    .in10(register_parallel_load_7_out_4), .in11(register_parallel_load_5_out_4),
    .in12(register_parallel_load_4_out_4), .in13(register_parallel_load_3_out_4),
    .in14(register_parallel_load_2_out_4), .in15(register_parallel_load_1_out_4), .out(Data_to_Read_2),
    .sel(Reg_No_2));
endmodule

module FullAdder1bit (
  input  a,
  input  b,
  input  carryIn,
  output carryOut,
  output sum
);

  wire and_1_out, and_2_out, and_3_out;

  and and_1 (and_1_out, a, b);
  and and_2 (and_2_out, b, carryIn);
  and and_3 (and_3_out, a, carryIn);
  xor xor_1 (sum, a, b, carryIn);
  or or_1 (carryOut, and_1_out, and_2_out, and_3_out);
endmodule

module HalfAdder (
  input  a,
  input  b,
  output sum,
  output carryout
);

  xor xor_1 (sum, a, b);
  and and_1 (carryout, a, b);
endmodule

module _2BitAdder (
  input  [1:0] a,
  input  [1:0] b,
  input  carryIn,
  output [1:0] sum,
  output carryOut
);

  wire fulladder1bit_1_carryout;

  FullAdder1bit fulladder1bit_1 (
    .a(a[0]), .b(b[0]), .carryIn(carryIn), .carryOut(fulladder1bit_1_carryout), .sum(sum[0]));
  FullAdder1bit fulladder1bit_2 (
    .a(a[1]), .b(b[1]), .carryIn(fulladder1bit_1_carryout), .carryOut(carryOut), .sum(sum[1]));

  // Notes on the sheet:
  //   2-Bit Adder
endmodule

module _18bitadder (
  input  carryIn,
  input  [17:0] operand_1,
  input  [17:0] operand_2,
  output [17:0] sum,
  output carryOut
);

  wire n2bitadder_1_carryout, n2bitadder_2_carryout, n2bitadder_3_carryout, n2bitadder_4_carryout,
       n2bitadder_5_carryout, n2bitadder_6_carryout, n2bitadder_7_carryout, n2bitadder_8_carryout;

  _2BitAdder u_2bitadder_1 (
    .a(operand_1[1:0]), .b(operand_2[1:0]), .carryIn(carryIn), .sum(sum[1:0]),
    .carryOut(n2bitadder_1_carryout));
  _2BitAdder u_2bitadder_2 (
    .a(operand_1[3:2]), .b(operand_2[3:2]), .carryIn(n2bitadder_1_carryout), .sum(sum[3:2]),
    .carryOut(n2bitadder_2_carryout));
  _2BitAdder u_2bitadder_3 (
    .a(operand_1[5:4]), .b(operand_2[5:4]), .carryIn(n2bitadder_2_carryout), .sum(sum[5:4]),
    .carryOut(n2bitadder_3_carryout));
  _2BitAdder u_2bitadder_4 (
    .a(operand_1[7:6]), .b(operand_2[7:6]), .carryIn(n2bitadder_3_carryout), .sum(sum[7:6]),
    .carryOut(n2bitadder_4_carryout));
  _2BitAdder u_2bitadder_5 (
    .a(operand_2[9:8]), .b(operand_1[9:8]), .carryIn(n2bitadder_4_carryout), .sum(sum[9:8]),
    .carryOut(n2bitadder_5_carryout));
  _2BitAdder u_2bitadder_6 (
    .a(operand_1[11:10]), .b(operand_2[11:10]), .carryIn(n2bitadder_5_carryout), .sum(sum[11:10]),
    .carryOut(n2bitadder_6_carryout));
  _2BitAdder u_2bitadder_7 (
    .a(operand_1[13:12]), .b(operand_2[13:12]), .carryIn(n2bitadder_6_carryout), .sum(sum[13:12]),
    .carryOut(n2bitadder_7_carryout));
  _2BitAdder u_2bitadder_8 (
    .a(operand_1[15:14]), .b(operand_2[15:14]), .carryIn(n2bitadder_7_carryout), .sum(sum[15:14]),
    .carryOut(n2bitadder_8_carryout));
  _2BitAdder u_2bitadder_9 (
    .a(operand_1[17:16]), .b(operand_2[17:16]), .carryIn(n2bitadder_8_carryout), .sum(sum[17:16]),
    .carryOut(carryOut));
endmodule

// Ext
module signExtender6To18bits (
  input  [5:0] immediate,
  output [17:0] output_extended_18bits
);


  assign output_extended_18bits = {{13{immediate[5]}}, immediate[4:0]};
endmodule

// Ext
module signExtention4To18Bits (
  input  [3:0] register,
  output [17:0] output_extended_18bits
);


  assign output_extended_18bits = {{15{register[3]}}, register[2:0]};
endmodule

module signExtention10To18Bits (
  input  [9:0] immediate,
  output [17:0] output_extended_18bits
);


  assign output_extended_18bits = {{9{immediate[9]}}, immediate[8:0]};
endmodule

module PC (
  input  [9:0] \input ,
  input  write,
  input  load,
  input  Clock,
  input  Jumps_Switch,
  output [17:0] \output 
);

  wire [17:0] adder18bits_1_p4, adder18bits_2_p4, bit_extender_1_out, bit_extender_2_out, multiplexer_1_out,
       multiplexer_2_out;

  assign bit_extender_1_out = {{17{1'b0}}, 1'b1};  // Bit_Extender bit_extender_1
  assign bit_extender_2_out = {{8{1'b0}}, \input };  // Bit_Extender bit_extender_2
  // Adder18Bits adder18bits_1: pin names not known; wires that end beside it: bit_extender_2_out, \output , 1'b0, adder18bits_1_p4
  // Adder18Bits adder18bits_2: pin names not known; wires that end beside it: bit_extender_1_out, \output , 1'b0, adder18bits_2_p4
  Multiplexer #(.width(18), .enable("false")) multiplexer_1 (
    .in0(adder18bits_1_p4), .in1(adder18bits_2_p4), .out(multiplexer_1_out), .sel(Jumps_Switch));
  Multiplexer #(.width(18), .enable("false")) multiplexer_2 (
    .in0(multiplexer_1_out), .in1({18{1'b0}}), .out(multiplexer_2_out), .sel(write));
  Register_Parallel_Load register_parallel_load_1 (
    .in_1(multiplexer_2_out), .load(load), .out_4(\output ), .clk(Clock));
endmodule

module Adder18Bits (
  input  [17:0] operand_1,
  input  [17:0] operand_2,
  output [17:0] sum,
  output carryOut
);

  wire n2bitadder_1_carryout, n2bitadder_2_carryout, n2bitadder_3_carryout, n2bitadder_4_carryout,
       n2bitadder_5_carryout, n2bitadder_6_carryout, n2bitadder_7_carryout, n2bitadder_8_carryout;

  _2BitAdder u_2bitadder_1 (
    .a(operand_1[1:0]), .b(operand_2[1:0]), .carryIn(1'b0), .sum(sum[1:0]), .carryOut(n2bitadder_1_carryout));
  _2BitAdder u_2bitadder_2 (
    .a(operand_1[3:2]), .b(operand_2[3:2]), .carryIn(n2bitadder_1_carryout), .sum(sum[3:2]),
    .carryOut(n2bitadder_2_carryout));
  _2BitAdder u_2bitadder_3 (
    .a(operand_1[5:4]), .b(operand_2[5:4]), .carryIn(n2bitadder_2_carryout), .sum(sum[5:4]),
    .carryOut(n2bitadder_3_carryout));
  _2BitAdder u_2bitadder_4 (
    .a(operand_1[7:6]), .b(operand_2[7:6]), .carryIn(n2bitadder_3_carryout), .sum(sum[7:6]),
    .carryOut(n2bitadder_4_carryout));
  _2BitAdder u_2bitadder_5 (
    .a(operand_2[9:8]), .b(operand_1[9:8]), .carryIn(n2bitadder_4_carryout), .sum(sum[9:8]),
    .carryOut(n2bitadder_5_carryout));
  _2BitAdder u_2bitadder_6 (
    .a(operand_1[11:10]), .b(operand_2[11:10]), .carryIn(n2bitadder_5_carryout), .sum(sum[11:10]),
    .carryOut(n2bitadder_6_carryout));
  _2BitAdder u_2bitadder_7 (
    .a(operand_1[13:12]), .b(operand_2[13:12]), .carryIn(n2bitadder_6_carryout), .sum(sum[13:12]),
    .carryOut(n2bitadder_7_carryout));
  _2BitAdder u_2bitadder_8 (
    .a(operand_1[15:14]), .b(operand_2[15:14]), .carryIn(n2bitadder_7_carryout), .sum(sum[15:14]),
    .carryOut(n2bitadder_8_carryout));
  _2BitAdder u_2bitadder_9 (
    .a(operand_1[17:16]), .b(operand_2[17:16]), .carryIn(n2bitadder_8_carryout), .sum(sum[17:16]),
    .carryOut(carryOut));
endmodule

module ALU (
  input  [17:0] a,
  input  [17:0] b,
  input  [1:0] _15th_14th_bit,
  output carryOut,
  output [17:0] result
);

  wire [17:0] adder18bits_1_sum, and_1_out, nand_1_out, nor_1_out;

  Adder18Bits adder18bits_1 (.operand_1(a), .operand_2(b), .carryOut(carryOut), .sum(adder18bits_1_sum));
  assign and_1_out = a & b;  // AND_Gate and_1, 18 bits wide
  assign nand_1_out = ~(a & b);  // NAND_Gate nand_1, 18 bits wide
  assign nor_1_out = ~(a | b);  // NOR_Gate nor_1, 18 bits wide
  Multiplexer #(.select(2), .width(18), .enable("false")) multiplexer_1 (
    .in0(adder18bits_1_sum), .in1(and_1_out), .in2(nand_1_out), .in3(nor_1_out), .out(result),
    .sel(_15th_14th_bit));
endmodule

module flag (
  input  in_1,
  input  load,
  input  clk,
  output out_4
);

  wire multiplexer_1_out;

  Multiplexer #(.enable("false")) multiplexer_1 (.in0(out_4), .in1(in_1), .out(multiplexer_1_out), .sel(load));
  D_Flip_Flop d_flip_flop_1 (.D(multiplexer_1_out), .Q(out_4), .Clk(clk));
endmodule

module circuit (
);

  wire [17:0] pc_1_output;

  PC pc_1 (.\output (pc_1_output));  // open: input, Jumps_Switch, write, Clock, load
  ROM #(.addrWidth(18), .dataWidth(18)) rom_1 (.addr(pc_1_output), .sel(1'b1));  // open: data

  // Notes on the sheet:
  //   INSTRUCTION MEMO
  //   contents of rom_1 (hex, n*v repeats v):
  //   187fe 840 1cff6 5001 1327b 9001 f909 243f2 4a05 283fc 2c303 3023a 343c1 383f1 20c09
endmodule

module Control_unit (
  input  clock,
  input  [17:0] instruction,
  output [17:0] fetchInstr,
  output [3:0] opcode,
  output ALU_en,
  output regWrite,
  output dataMemRead,
  output dataMemWrite,
  output cmp,
  output jmp_en
);

  wire comparator_1_carry_flag, comparator_1_zero_flag, decoder_1_out0, decoder_1_out1, decoder_1_out2,
       decoder_1_out3, decoder_1_out4, decoder_1_out5, decoder_1_out9, decoder_1_out10, decoder_1_out11,
       decoder_1_out12, decoder_1_out13, decoder_1_out14, JA_out, JAE_out, JB_out, JBE_out, JE_out, Z_C_out,
       Z_C_prime_out;
  wire [17:0] signextention4to18bits_1_output_extended_18bits,
       signextention4to18bits_2_output_extended_18bits;

  PC pc_1 (
    .\input (instruction[9:0]), .\output (fetchInstr), .Jumps_Switch(jmp_en), .Clock(clock));  // open: write, load
  signExtention4To18Bits signextention4to18bits_1 (
    .register(instruction[3:0]), .output_extended_18bits(signextention4to18bits_1_output_extended_18bits));
  signExtention4To18Bits signextention4to18bits_2 (
    .register(instruction[13:10]), .output_extended_18bits(signextention4to18bits_2_output_extended_18bits));
  Decoder #(.select(4), .enable("false")) decoder_1 (
    .out0(decoder_1_out0), .out1(decoder_1_out1), .out2(decoder_1_out2), .out3(decoder_1_out3),
    .out4(decoder_1_out4), .out5(decoder_1_out5), .out6(dataMemRead), .out7(dataMemWrite), .out8(cmp),
    .out9(decoder_1_out9), .out10(decoder_1_out10), .out11(decoder_1_out11), .out12(decoder_1_out12),
    .out13(decoder_1_out13), .out14(decoder_1_out14), .sel(instruction[17:14]));  // open: out15
  Comparator comparator_1 (
    .number_1(signextention4to18bits_2_output_extended_18bits),
    .number_2(signextention4to18bits_1_output_extended_18bits), .CARRY_FLAG(comparator_1_carry_flag),
    .ZERO_FLAG(comparator_1_zero_flag));
  or or_1 (ALU_en, decoder_1_out0, decoder_1_out1, decoder_1_out2, decoder_1_out3, decoder_1_out4, decoder_1_out5);
  and JE (JE_out, decoder_1_out10, comparator_1_zero_flag, ~comparator_1_carry_flag);  // AND_Gate
  and JA (JA_out, decoder_1_out11, ~comparator_1_zero_flag, ~comparator_1_carry_flag);  // AND_Gate
  and JB (JB_out, decoder_1_out12, ~comparator_1_zero_flag, comparator_1_carry_flag);  // AND_Gate
  or Z_C_prime (Z_C_prime_out, comparator_1_zero_flag, ~comparator_1_carry_flag);  // OR_Gate
  or Z_C (Z_C_out, comparator_1_zero_flag, comparator_1_carry_flag);
  or or_2 (regWrite, ALU_en, dataMemRead);
  and JAE (JAE_out, decoder_1_out13, Z_C_prime_out);
  and JBE (JBE_out, decoder_1_out14, Z_C_out);
  or or_3 (jmp_en, decoder_1_out9, JE_out, JA_out, JB_out, JAE_out, JBE_out);

  assign opcode = instruction[17:14];

  // Other names for the same wires on the sheet: address[9:0] = instruction[9:0]; immediate[5:0] = instruction[5:0];
  //   Operand_SrcRegister2[3:0] = instruction[3:0]; Operand_DestRegister1[3:0] = instruction[13:10];
  //   SrcRegister1[3:0] = instruction[9:6]

  // Notes on the sheet:
  //   ADD
  //   AND
  //   NAND
  //   NOR
  //   ADDI
  //   ANDI
  //   LD
  //   ST
  //   CMP
  //   JUMP
  //   JE
  //   JA
  //   JB
  //   JAE
  //   JBE
endmodule
